# Fritzing sketch Final Project Schematic (saved by Fritzing 0.9.3b)
breadboards: 1

parts:
  S1 = Pushbutton [package="[THT]"]
  Part1 = Arduino Uno (Rev3) - ICSP  # not connected
  R1 = Basic Flex Resistor
  LED1 = LED_RING [package=led_ring]
  Part2 = Memoire 1.0 - SD card log shield
  M1 = Stepper Motor - Unipolar
  IC1 = ULN2003A [package="DIP16 [THT]"]
  R2 = Resistor [tolerance=±5% resistance=220 package=THT]
  R3 = Resistor [tolerance=±5% resistance=220 package=THT]

nets:
  N1: S1.Pin_1, S1.Pin_2, R1.pin_1, LED1.6, Part2.+5V, M1.COMMON_2, R2.Pin_1
  N2: S1.Pin_3, S1.Pin_4, Part2.DIG_7, R3.Pin_1
  N3: R1.Pin_2, Part2.A_IN_1, R2.Pin_0
  N4: LED1.COM0, Part2.GND, M1.D, R3.Pin_0
  N5: LED1.16, Part2.DIG_6
  N6: Part2.DIG_8, IC1.Out_5
  N7: Part2.DIG_10, Part2.DIG_2, Part2.DIG_4, Part2.DIG_0
  N8: Part2.DIG_11, IC1.Out_4
  N9: Part2.DIG_12, IC1.Out_3
  N10: Part2.DIG_13, IC1.Out_1
  N11: Part2.DIG_1, Part2.DIG_3, Part2.DIG_5

notes:
  [Adafruit Wave Shield W/ Arduino Uno]
  [Neopixel Ring ]
  Hook input into PIN 6
  GND to GND
  VCC to VCC
  [Flex Sensor]
  Hook to PIN A0
  [Stepper Motor]
  VCC to VCC
  GND to GND
  INT 1 to PIN 8
  INT 2 to PIN 11
  INT 3 to PIN 12
  INT 4 to PIN 13
  [Stepper Motor Driver]
  [Push-button]
